// Logisim project cpu.circ as structural Verilog
module adder_half (
  input  A,
  input  B,
  output SUM,
  output CARRY
);

  xor xor_1 (SUM, A, B);
  and and_1 (CARRY, A, B);
endmodule

module adder_full (
  input  A,
  input  B,
  input  C_IN,
  output SUM,
  output C_OUT
);

  wire adder_half_1_carry, adder_half_1_sum, adder_half_2_carry;

  adder_half adder_half_1 (.A(A), .B(B), .SUM(adder_half_1_sum), .CARRY(adder_half_1_carry));
  adder_half adder_half_2 (.A(adder_half_1_sum), .B(C_IN), .SUM(SUM), .CARRY(adder_half_2_carry));
  or or_1 (C_OUT, adder_half_1_carry, adder_half_2_carry);
endmodule

module adder_4bit (
  input  C_IN,
  input  [3:0] A,
  input  [3:0] B,
  output [3:0] SUM,
  output C_OUT
);

  wire adder_full_1_c_out, adder_full_2_c_out, adder_full_3_c_out;

  adder_full adder_full_1 (.C_OUT(adder_full_1_c_out), .SUM(SUM[0]), .A(C_IN), .B(A[0]), .C_IN(B[0]));
  adder_full adder_full_2 (.C_OUT(adder_full_2_c_out), .SUM(SUM[1]), .A(adder_full_1_c_out), .B(A[1]), .C_IN(B[1]));
  adder_full adder_full_3 (.C_OUT(adder_full_3_c_out), .SUM(SUM[2]), .A(adder_full_2_c_out), .B(A[2]), .C_IN(B[2]));
  adder_full adder_full_4 (.C_OUT(C_OUT), .SUM(SUM[3]), .A(adder_full_3_c_out), .B(A[3]), .C_IN(B[3]));
endmodule

// FA
module adder_8bit (
  input  C_IN,
  input  [7:0] A,
  input  [7:0] B,
  output [7:0] SUM,
  output OVERFLOW
);

  wire adder_4bit_1_c_out;

  adder_4bit adder_4bit_1 (.C_IN(C_IN), .A(A[3:0]), .B(B[3:0]), .SUM(SUM[3:0]), .C_OUT(adder_4bit_1_c_out));
  adder_4bit adder_4bit_2 (.C_IN(adder_4bit_1_c_out), .A(A[7:4]), .B(B[7:4]), .SUM(SUM[7:4]), .C_OUT(OVERFLOW));
endmodule

module ALU (
  input  A_0,
  input  A_1,
  input  A_2,
  input  A_3,
  input  A_4,
  input  A_5,
  input  A_6,
  input  A_7,
  input  EO,
  input  B_0,
  input  B_1,
  input  B_2,
  input  SU,
  input  FI,
  input  B_3,
  input  B_4,
  input  B_5,
  input  B_6,
  input  B_7,
  output ZF,
  output [7:0] DEBUG,
  output OUT_0,
  output OUT_1,
  output OUT_2,
  output OUT_3,
  output OUT_4,
  output OUT_5,
  output CF,
  output OUT_6,
  output OUT_7
);

  wire clock_1_out;
  wire [7:0] bit_extender_1_out, register_1_q, xor_1_out;

  assign bit_extender_1_out = {{7{SU}}, SU};  // Bit_Extender bit_extender_1
  assign xor_1_out = {B_7, B_6, B_5, B_4, B_3, B_2, B_1, B_0} ^ bit_extender_1_out;  // XOR_Gate xor_1, 8 bits wide
  adder_8bit adder_8bit_1 (
    .C_IN(SU), .A({A_7, A_6, A_5, A_4, A_3, A_2, A_1, A_0}), .B(xor_1_out), .SUM(DEBUG), .OVERFLOW(CF));
  Clock clock_1 (.out(clock_1_out));
  assign {OUT_7, OUT_6, OUT_5, OUT_4, OUT_3, OUT_2, OUT_1, OUT_0} = EO ? register_1_q : 8'bz;  // Controlled_Buffer controlled_buffer_1
  Register register_1 (.D(DEBUG), .Q(register_1_q), .clk(clock_1_out));  // open: en, clr
  nor nor_1 (ZF, DEBUG[0], DEBUG[1], DEBUG[2], DEBUG[3], DEBUG[4], DEBUG[5], DEBUG[6], DEBUG[7]);
endmodule

module register_1bit (
  input  CLK,
  input  D,
  input  LOAD,
  input  EN,
  output Q
);

  wire and_1_out, and_2_out, not_1_out, or_1_out, Q_t;

  and and_1 (and_1_out, D, LOAD);
  not not_1 (not_1_out, LOAD);
  or or_1 (or_1_out, and_1_out, and_2_out);
  and and_2 (and_2_out, Q_t, not_1_out);
  d_flip_flop d_flip_flop_1 (.CLK(CLK), .D(or_1_out), .Q(Q_t));  // open: Q_NOT
  assign Q = EN ? Q_t : 1'bz;  // Controlled_Buffer controlled_buffer_1
endmodule

module d_flip_flop (
  input  CLK,
  input  D,
  output Q,
  output Q_NOT
);

  wire and_1_out, and_2_out, not_1_out;

  not not_1 (not_1_out, D);
  and and_1 (and_1_out, not_1_out, CLK);
  and and_2 (and_2_out, CLK, D);
  nor nor_1 (Q, and_1_out, Q_NOT);
  nor nor_2 (Q_NOT, Q, and_2_out);
endmodule

module register_8bit_diy (
  input  [7:0] D,
  input  CLK,
  input  LOAD,
  input  EN,
  output [7:0] Q
);

  register_1bit register_1bit_1 (.CLK(CLK), .D(D[7]), .LOAD(LOAD), .EN(EN), .Q(Q[7]));
  register_1bit register_1bit_2 (.CLK(CLK), .D(D[6]), .LOAD(LOAD), .EN(EN), .Q(Q[6]));
  register_1bit register_1bit_3 (.CLK(CLK), .D(D[5]), .LOAD(LOAD), .EN(EN), .Q(Q[5]));
  register_1bit register_1bit_4 (.CLK(CLK), .D(D[4]), .LOAD(LOAD), .EN(EN), .Q(Q[4]));
  register_1bit register_1bit_5 (.CLK(CLK), .D(D[3]), .LOAD(LOAD), .EN(EN), .Q(Q[3]));
  register_1bit register_1bit_6 (.CLK(CLK), .D(D[2]), .LOAD(LOAD), .EN(EN), .Q(Q[2]));
  register_1bit register_1bit_7 (.CLK(CLK), .D(D[1]), .LOAD(LOAD), .EN(EN), .Q(Q[1]));
  register_1bit register_1bit_8 (.CLK(CLK), .D(D[0]), .LOAD(LOAD), .EN(EN), .Q(Q[0]));
endmodule

module A (
  input  IN_0,
  input  IN_1,
  input  IN_2,
  input  IN_3,
  input  IN_4,
  input  LOAD,
  input  IN_5,
  input  IN_6,
  input  ENABLE,
  input  IN_7,
  output OUT_0,
  output OUT_1,
  output OUT_2,
  output OUT_3,
  output OUT_4,
  output OUT_5,
  output OUT_6,
  output OUT_7,
  output [7:0] DEBUG,
  output Q_0,
  output Q_1,
  output Q_2,
  output Q_3,
  output Q_4,
  output Q_5,
  output Q_6,
  output Q_7
);

  wire clock_1_out;

  Clock clock_1 (.out(clock_1_out));
  Register register_1 (
    .D({IN_7, IN_6, IN_5, IN_4, IN_3, IN_2, IN_1, IN_0}), .en(LOAD), .Q(DEBUG), .clk(clock_1_out));  // open: clr
  assign {OUT_7, OUT_6, OUT_5, OUT_4, OUT_3, OUT_2, OUT_1, OUT_0} = ENABLE ? DEBUG : 8'bz;  // Controlled_Buffer controlled_buffer_1

  assign Q_0 = DEBUG[0];
  assign Q_1 = DEBUG[1];
  assign Q_2 = DEBUG[2];
  assign Q_3 = DEBUG[3];
  assign Q_4 = DEBUG[4];
  assign Q_5 = DEBUG[5];
  assign Q_6 = DEBUG[6];
  assign Q_7 = DEBUG[7];
endmodule

module multiplexor_4bit (
  input  IN,
  input  [3:0] ADDRESS,
  output [15:0] OUT
);

  wire NA0, NA1, NA2, NA3;

  // Probe on ADDRESS
  not not_1 (NA0, ADDRESS[0]);
  not not_2 (NA1, ADDRESS[1]);
  not not_3 (NA2, ADDRESS[2]);
  not not_4 (NA3, ADDRESS[3]);
  and and_1 (OUT[0], NA0, NA1, NA2, NA3, IN);
  and and_2 (OUT[1], ADDRESS[0], NA1, NA2, NA3, IN);
  and and_3 (OUT[2], NA0, ADDRESS[1], NA2, NA3, IN);
  and and_4 (OUT[3], ADDRESS[0], ADDRESS[1], NA2, NA3, IN);
  and and_5 (OUT[4], NA0, NA1, ADDRESS[2], NA3, IN);
  and and_6 (OUT[5], ADDRESS[0], NA1, ADDRESS[2], NA3, IN);
  and and_7 (OUT[6], NA0, ADDRESS[1], ADDRESS[2], NA3, IN);
  and and_8 (OUT[7], ADDRESS[0], ADDRESS[1], ADDRESS[2], NA3, IN);
  and and_9 (OUT[8], NA0, NA1, NA2, ADDRESS[3], IN);
  and and_10 (OUT[9], ADDRESS[0], NA1, NA2, ADDRESS[3], IN);
  and and_11 (OUT[10], NA0, ADDRESS[1], NA2, ADDRESS[3], IN);
  and and_12 (OUT[11], ADDRESS[0], ADDRESS[1], NA2, ADDRESS[3], IN);
  and and_13 (OUT[12], NA0, NA1, ADDRESS[2], ADDRESS[3], IN);
  and and_14 (OUT[13], ADDRESS[0], NA1, ADDRESS[2], ADDRESS[3], IN);
  and and_15 (OUT[14], NA0, ADDRESS[1], ADDRESS[2], ADDRESS[3], IN);
  and and_16 (OUT[15], ADDRESS[0], ADDRESS[1], ADDRESS[2], ADDRESS[3], IN);

  // Other names for the same wires on the sheet: A0 = ADDRESS[0]; A1 = ADDRESS[1]; A2 = ADDRESS[2]; A3 = ADDRESS[3]
endmodule

module RAM_diy (
  input  CLK,
  input  [7:0] D,
  input  LOAD,
  input  [3:0] ADDRESS,
  input  EN,
  output [7:0] Q
);

  wire a_1_p6, a_1_p7, a_2_p16, a_2_p17, a_3_p16, a_3_p17, a_4_p16, a_4_p17, a_5_p16, a_5_p17, a_6_p16,
       a_6_p17, a_7_p16, a_7_p17, a_8_p16, a_8_p17, a_9_p16, a_9_p17, a_10_p16, a_10_p17, a_11_p16, a_11_p17,
       a_12_p16, a_12_p17, a_13_p16, a_13_p17, a_14_p16, a_14_p17, a_15_p16, a_15_p17;
  wire [15:0] multiplexor_4bit_1_out, multiplexor_4bit_2_out;

  multiplexor_4bit multiplexor_4bit_1 (.IN(LOAD), .ADDRESS(ADDRESS), .OUT(multiplexor_4bit_1_out));
  multiplexor_4bit multiplexor_4bit_2 (.IN(EN), .ADDRESS(ADDRESS), .OUT(multiplexor_4bit_2_out));
  // A a_1: pin names not known; wires that end beside it: D, multiplexor_4bit_1_out[0], CLK, multiplexor_4bit_2_out[0], Q, a_1_p6, a_1_p7, D
  // A a_2: pin names not known; wires that end beside it: multiplexor_4bit_1_out[0], CLK, multiplexor_4bit_2_out[0], multiplexor_4bit_2_out[0], multiplexor_4bit_2_out[0], multiplexor_4bit_2_out[0], Q, a_1_p6, a_1_p7, Q, D, multiplexor_4bit_1_out[1], CLK, multiplexor_4bit_2_out[1], Q, a_2_p16, a_2_p17, D
  // A a_3: pin names not known; wires that end beside it: multiplexor_4bit_1_out[1], CLK, multiplexor_4bit_2_out[1], multiplexor_4bit_2_out[1], multiplexor_4bit_2_out[1], multiplexor_4bit_2_out[1], Q, a_2_p16, a_2_p17, Q, D, multiplexor_4bit_1_out[2], CLK, multiplexor_4bit_2_out[2], Q, a_3_p16, a_3_p17, D
  // A a_4: pin names not known; wires that end beside it: multiplexor_4bit_1_out[2], CLK, multiplexor_4bit_2_out[2], multiplexor_4bit_2_out[2], multiplexor_4bit_2_out[2], multiplexor_4bit_2_out[2], Q, a_3_p16, a_3_p17, Q, D, multiplexor_4bit_1_out[3], CLK, multiplexor_4bit_2_out[3], Q, a_4_p16, a_4_p17, D
  // A a_5: pin names not known; wires that end beside it: multiplexor_4bit_1_out[3], CLK, multiplexor_4bit_2_out[3], multiplexor_4bit_2_out[3], multiplexor_4bit_2_out[3], multiplexor_4bit_2_out[3], Q, a_4_p16, a_4_p17, Q, D, multiplexor_4bit_1_out[4], CLK, multiplexor_4bit_2_out[4], Q, a_5_p16, a_5_p17, D
  // A a_6: pin names not known; wires that end beside it: multiplexor_4bit_1_out[4], CLK, multiplexor_4bit_2_out[4], multiplexor_4bit_2_out[4], multiplexor_4bit_2_out[4], multiplexor_4bit_2_out[4], Q, a_5_p16, a_5_p17, Q, D, multiplexor_4bit_1_out[5], CLK, multiplexor_4bit_2_out[5], Q, a_6_p16, a_6_p17, D
  // A a_7: pin names not known; wires that end beside it: multiplexor_4bit_1_out[5], CLK, multiplexor_4bit_2_out[5], multiplexor_4bit_2_out[5], multiplexor_4bit_2_out[5], multiplexor_4bit_2_out[5], Q, a_6_p16, a_6_p17, Q, D, multiplexor_4bit_1_out[6], CLK, multiplexor_4bit_2_out[6], Q, a_7_p16, a_7_p17, D
  // A a_8: pin names not known; wires that end beside it: multiplexor_4bit_1_out[6], CLK, multiplexor_4bit_2_out[6], multiplexor_4bit_2_out[6], multiplexor_4bit_2_out[6], multiplexor_4bit_2_out[6], Q, a_7_p16, a_7_p17, Q, D, multiplexor_4bit_1_out[7], CLK, multiplexor_4bit_2_out[7], Q, a_8_p16, a_8_p17, D
  // A a_9: pin names not known; wires that end beside it: multiplexor_4bit_1_out[7], CLK, multiplexor_4bit_2_out[7], multiplexor_4bit_2_out[7], multiplexor_4bit_2_out[7], multiplexor_4bit_2_out[7], Q, a_8_p16, a_8_p17, Q, D, multiplexor_4bit_1_out[8], CLK, multiplexor_4bit_2_out[8], Q, a_9_p16, a_9_p17, D
  // A a_10: pin names not known; wires that end beside it: multiplexor_4bit_1_out[8], CLK, multiplexor_4bit_2_out[8], multiplexor_4bit_2_out[8], multiplexor_4bit_2_out[8], multiplexor_4bit_2_out[8], Q, a_9_p16, a_9_p17, Q, D, multiplexor_4bit_1_out[9], CLK, multiplexor_4bit_2_out[9], Q, a_10_p16, a_10_p17, D
  // A a_11: pin names not known; wires that end beside it: multiplexor_4bit_1_out[9], CLK, multiplexor_4bit_2_out[9], multiplexor_4bit_2_out[9], multiplexor_4bit_2_out[9], multiplexor_4bit_2_out[9], Q, a_10_p16, a_10_p17, Q, D, multiplexor_4bit_1_out[10], CLK, multiplexor_4bit_2_out[10], Q, a_11_p16, a_11_p17, D
  // A a_12: pin names not known; wires that end beside it: multiplexor_4bit_1_out[10], CLK, multiplexor_4bit_2_out[10], multiplexor_4bit_2_out[10], multiplexor_4bit_2_out[10], multiplexor_4bit_2_out[10], Q, a_11_p16, a_11_p17, Q, D, multiplexor_4bit_1_out[11], CLK, multiplexor_4bit_2_out[11], Q, a_12_p16, a_12_p17, D
  // A a_13: pin names not known; wires that end beside it: multiplexor_4bit_1_out[11], CLK, multiplexor_4bit_2_out[11], multiplexor_4bit_2_out[11], multiplexor_4bit_2_out[11], multiplexor_4bit_2_out[11], Q, a_12_p16, a_12_p17, Q, D, multiplexor_4bit_1_out[12], CLK, multiplexor_4bit_2_out[12], Q, a_13_p16, a_13_p17, D
  // A a_14: pin names not known; wires that end beside it: multiplexor_4bit_1_out[12], CLK, multiplexor_4bit_2_out[12], multiplexor_4bit_2_out[12], multiplexor_4bit_2_out[12], multiplexor_4bit_2_out[12], Q, a_13_p16, a_13_p17, Q, D, multiplexor_4bit_1_out[13], CLK, multiplexor_4bit_2_out[13], Q, a_14_p16, a_14_p17, D
  // A a_15: pin names not known; wires that end beside it: multiplexor_4bit_1_out[13], CLK, multiplexor_4bit_2_out[13], multiplexor_4bit_2_out[13], multiplexor_4bit_2_out[13], multiplexor_4bit_2_out[13], Q, a_14_p16, a_14_p17, Q, D, multiplexor_4bit_1_out[14], CLK, multiplexor_4bit_2_out[14], Q, a_15_p16, a_15_p17, D
  // A a_16: pin names not known; wires that end beside it: multiplexor_4bit_1_out[14], CLK, multiplexor_4bit_2_out[14], multiplexor_4bit_2_out[14], multiplexor_4bit_2_out[14], multiplexor_4bit_2_out[14], Q, a_15_p16, a_15_p17, Q, D, multiplexor_4bit_1_out[15], CLK, multiplexor_4bit_2_out[15], Q
endmodule

// CNT
module counter_4bit (
  input  CLK,
  input  ENABLE,
  input  [3:0] IN,
  output [3:0] OUT
);

  wire j_k_ff_1_qn, j_k_ff_2_qn, j_k_ff_3_qn;
  wire [3:0] not_1_out;

  assign not_1_out = ~IN;  // NOT_Gate not_1, 4 bits wide
  J_K_Flip_Flop j_k_ff_1 (
    .J(1'b1), .clk(CLK), .K(1'b1), .Q(OUT[0]), .Qn(j_k_ff_1_qn), .preset(IN[3]), .en(ENABLE),
    .reset(not_1_out[3]));
  J_K_Flip_Flop j_k_ff_2 (
    .J(1'b1), .clk(j_k_ff_1_qn), .K(1'b1), .Q(OUT[1]), .Qn(j_k_ff_2_qn), .preset(IN[2]), .en(ENABLE),
    .reset(not_1_out[2]));
  J_K_Flip_Flop j_k_ff_3 (
    .J(1'b1), .clk(j_k_ff_2_qn), .K(1'b1), .Q(OUT[2]), .Qn(j_k_ff_3_qn), .preset(IN[1]), .en(ENABLE),
    .reset(not_1_out[1]));
  J_K_Flip_Flop j_k_ff_4 (
    .J(1'b1), .clk(j_k_ff_3_qn), .K(1'b1), .Q(OUT[3]), .preset(IN[0]), .en(ENABLE), .reset(not_1_out[0]));  // open: Qn
endmodule

module CPU (
  input  in_1,
  input  CO,
  input  MI,
  input  J,
  input  CE,
  input  RI,
  input  RO,
  input  AI,
  input  AO,
  input  EO,
  input  II,
  input  SU,
  input  IO,
  input  FI,
  input  BI,
  input  BO,
  input  OI,
  input  [7:0] in_18,
  input  in_19
);

  wire a_1_q_0, a_1_q_1, a_1_q_2, a_1_q_3, a_1_q_4, a_1_q_5, a_1_q_6, a_1_q_7, alu_1_cf, alu_1_zf, and_1_out,
       b_1_q_0, b_1_q_1, b_1_q_2, b_1_q_3, b_1_q_4, b_1_q_5, b_1_q_6, b_1_q_7, clock_1_out, ir_1_q_0,
       ir_1_q_1, ir_1_q_2, ir_1_q_3, ir_1_q_4, ir_1_q_5, ir_1_q_6, ir_1_q_7, mar_1_out_0, mar_1_out_1,
       mar_1_out_2, mar_1_out_3;
  wire [3:0] mar_1_debug, pc_1_debug;
  wire [7:0] b_1_debug, ir_1_debug, out_1_debug, ram_1_debug, ram_1_out_0;

  Clock clock_1 (.out(clock_1_out));
  and and_1 (and_1_out, clock_1_out, ~in_1);  // AND_Gate
  // Probe on mar_1_debug
  LED u_MI (.in(MI));
  RAM ram_1 (
    .A_0(mar_1_out_0), .A_1(mar_1_out_1), .A_2(mar_1_out_2), .A_3(mar_1_out_3), .IN_0(ram_1_out_0[0]),
    .IN_1(ram_1_out_0[1]), .IN_2(ram_1_out_0[2]), .IN_3(ram_1_out_0[3]), .IN_4(ram_1_out_0[4]),
    .IN_5(ram_1_out_0[5]), .IN_6(ram_1_out_0[6]), .IN_7(ram_1_out_0[7]), .OUT_0(ram_1_out_0[0]),
    .OUT_1(ram_1_out_0[1]), .OUT_2(ram_1_out_0[2]), .OUT_3(ram_1_out_0[3]), .OUT_4(ram_1_out_0[4]),
    .OUT_5(ram_1_out_0[5]), .OUT_6(ram_1_out_0[6]), .OUT_7(ram_1_out_0[7]), .RI(RI), .DEBUG(ram_1_debug),
    .RO(RO));
  // Probe on ram_1_debug
  IR ir_1 (
    .DEBUG(ir_1_debug), .II(II), .IO(IO), .IN_0(ram_1_out_0[0]), .IN_1(ram_1_out_0[1]),
    .IN_2(ram_1_out_0[2]), .IN_3(ram_1_out_0[3]), .IN_4(ram_1_out_0[4]), .IN_5(ram_1_out_0[5]),
    .IN_6(ram_1_out_0[6]), .IN_7(ram_1_out_0[7]), .OUT_0(ram_1_out_0[0]), .OUT_1(ram_1_out_0[1]),
    .OUT_2(ram_1_out_0[2]), .OUT_3(ram_1_out_0[3]), .OUT_4(ram_1_out_0[4]), .OUT_5(ram_1_out_0[5]),
    .OUT_6(ram_1_out_0[6]), .OUT_7(ram_1_out_0[7]), .Q_0(ir_1_q_0), .Q_1(ir_1_q_1), .Q_2(ir_1_q_2),
    .Q_3(ir_1_q_3), .Q_4(ir_1_q_4), .Q_5(ir_1_q_5), .Q_6(ir_1_q_6), .Q_7(ir_1_q_7));  // open: CLK
  // Probe on ir_1_debug
  MAR mar_1 (
    .IN_0(ram_1_out_0[0]), .IN_1(ram_1_out_0[1]), .IN_2(ram_1_out_0[2]), .IN_3(ram_1_out_0[3]),
    .OUT_0(mar_1_out_0), .OUT_1(mar_1_out_1), .OUT_2(mar_1_out_2), .OUT_3(mar_1_out_3), .MI(MI),
    .DEBUG(mar_1_debug), .CLK(and_1_out));
  // Probe on ram_1_out_0
  assign ram_1_out_0 = in_19 ? in_18 : 8'bz;  // Controlled_Buffer controlled_buffer_1
  Pull_Resistor pull_resistor_1 (.node(ram_1_out_0));
  // Probe on pc_1_debug
  PC pc_1 (
    .IN_0(ram_1_out_0[0]), .IN_1(ram_1_out_0[1]), .IN_2(ram_1_out_0[2]), .IN_3(ram_1_out_0[3]),
    .OUT_0(ram_1_out_0[0]), .OUT_1(ram_1_out_0[1]), .OUT_2(ram_1_out_0[2]), .OUT_3(ram_1_out_0[3]), .J(J),
    .CE(CE), .CO(CO), .DEBUG(pc_1_debug), .CLK(and_1_out));
  A a_1 (
    .LOAD(AI), .ENABLE(AO), .IN_0(ram_1_out_0[0]), .IN_1(ram_1_out_0[1]), .IN_2(ram_1_out_0[2]),
    .IN_3(ram_1_out_0[3]), .IN_4(ram_1_out_0[4]), .IN_5(ram_1_out_0[5]), .IN_6(ram_1_out_0[6]),
    .IN_7(ram_1_out_0[7]), .OUT_0(ram_1_out_0[0]), .OUT_1(ram_1_out_0[1]), .OUT_2(ram_1_out_0[2]),
    .OUT_3(ram_1_out_0[3]), .OUT_4(ram_1_out_0[4]), .OUT_5(ram_1_out_0[5]), .OUT_6(ram_1_out_0[6]),
    .OUT_7(ram_1_out_0[7]), .Q_0(a_1_q_0), .Q_1(a_1_q_1), .Q_2(a_1_q_2), .Q_3(a_1_q_3), .Q_4(a_1_q_4),
    .Q_5(a_1_q_5), .Q_6(a_1_q_6), .Q_7(a_1_q_7));  // open: DEBUG
  // Probe on nothing
  ALU alu_1 (
    .SU(SU), .A_0(a_1_q_0), .A_1(a_1_q_1), .A_2(a_1_q_2), .A_3(a_1_q_3), .A_4(a_1_q_4), .A_5(a_1_q_5),
    .A_6(a_1_q_6), .A_7(a_1_q_7), .B_0(b_1_q_0), .B_1(b_1_q_1), .B_2(b_1_q_2), .B_3(b_1_q_3), .B_4(b_1_q_4),
    .B_5(b_1_q_5), .B_6(b_1_q_6), .B_7(b_1_q_7), .FI(FI), .EO(EO), .OUT_0(ram_1_out_0[0]),
    .OUT_1(ram_1_out_0[1]), .OUT_2(ram_1_out_0[2]), .OUT_3(ram_1_out_0[3]), .OUT_4(ram_1_out_0[4]),
    .OUT_5(ram_1_out_0[5]), .OUT_6(ram_1_out_0[6]), .OUT_7(ram_1_out_0[7]), .CF(alu_1_cf), .ZF(alu_1_zf));  // open: DEBUG
  // Probe on nothing
  LED CF (.in(alu_1_cf));
  LED ZF (.in(alu_1_zf));
  // Probe on b_1_debug
  B b_1 (
    .IN_0(ram_1_out_0[0]), .IN_1(ram_1_out_0[1]), .IN_2(ram_1_out_0[2]), .IN_3(ram_1_out_0[3]),
    .IN_4(ram_1_out_0[4]), .LOAD(BI), .IN_5(ram_1_out_0[5]), .IN_6(ram_1_out_0[6]), .IN_7(ram_1_out_0[7]),
    .OUT_0(ram_1_out_0[0]), .OUT_1(ram_1_out_0[1]), .OUT_2(ram_1_out_0[2]), .OUT_3(ram_1_out_0[3]),
    .OUT_4(ram_1_out_0[4]), .OUT_5(ram_1_out_0[5]), .OUT_6(ram_1_out_0[6]), .OUT_7(ram_1_out_0[7]),
    .DEBUG(b_1_debug), .Q_0(b_1_q_0), .Q_1(b_1_q_1), .Q_2(b_1_q_2), .Q_3(b_1_q_3), .Q_4(b_1_q_4),
    .Q_5(b_1_q_5), .Q_6(b_1_q_6), .Q_7(b_1_q_7), .ENABLE(BO));
  OUT out_1 (
    .IN_0(ram_1_out_0[0]), .IN_1(ram_1_out_0[1]), .IN_2(ram_1_out_0[2]), .IN_3(ram_1_out_0[3]),
    .IN_4(ram_1_out_0[4]), .LOAD(OI), .IN_5(ram_1_out_0[5]), .IN_6(ram_1_out_0[6]), .IN_7(ram_1_out_0[7]),
    .DEBUG(out_1_debug));
  // Probe on out_1_debug
endmodule

module PC (
  input  IN_0,
  input  IN_1,
  input  IN_2,
  input  J,
  input  IN_3,
  input  CLK,
  input  CE,
  input  CO,
  output [3:0] DEBUG,
  output OUT_0,
  output OUT_1,
  output OUT_2,
  output OUT_3
);

  wire [3:0] controlled_buffer_1_out;

  assign controlled_buffer_1_out = J ? {IN_3, IN_2, IN_1, IN_0} : 4'bz;  // Controlled_Buffer controlled_buffer_1
  assign {OUT_3, OUT_2, OUT_1, OUT_0} = CO ? DEBUG : 4'bz;  // Controlled_Buffer controlled_buffer_2
  counter_4bit counter_4bit_1 (.ENABLE(CE), .IN(controlled_buffer_1_out), .OUT(DEBUG), .CLK(CLK));
endmodule

module B (
  input  IN_0,
  input  IN_1,
  input  IN_2,
  input  IN_3,
  input  IN_4,
  input  LOAD,
  input  IN_5,
  input  IN_6,
  input  ENABLE,
  input  IN_7,
  output OUT_0,
  output OUT_1,
  output OUT_2,
  output OUT_3,
  output OUT_4,
  output OUT_5,
  output OUT_6,
  output OUT_7,
  output [7:0] DEBUG,
  output Q_0,
  output Q_1,
  output Q_2,
  output Q_3,
  output Q_4,
  output Q_5,
  output Q_6,
  output Q_7
);

  wire clock_1_out;

  Clock clock_1 (.out(clock_1_out));
  Register register_1 (
    .D({IN_7, IN_6, IN_5, IN_4, IN_3, IN_2, IN_1, IN_0}), .en(LOAD), .Q(DEBUG), .clk(clock_1_out));  // open: clr
  assign {OUT_7, OUT_6, OUT_5, OUT_4, OUT_3, OUT_2, OUT_1, OUT_0} = ENABLE ? DEBUG : 8'bz;  // Controlled_Buffer controlled_buffer_1

  assign Q_0 = DEBUG[0];
  assign Q_1 = DEBUG[1];
  assign Q_2 = DEBUG[2];
  assign Q_3 = DEBUG[3];
  assign Q_4 = DEBUG[4];
  assign Q_5 = DEBUG[5];
  assign Q_6 = DEBUG[6];
  assign Q_7 = DEBUG[7];
endmodule

module OUT (
  input  IN_0,
  input  IN_1,
  input  IN_2,
  input  IN_3,
  input  IN_4,
  input  LOAD,
  input  IN_5,
  input  IN_6,
  input  IN_7,
  output [7:0] DEBUG
);

  wire clock_1_out;

  Clock clock_1 (.out(clock_1_out));
  Register register_1 (
    .D({IN_7, IN_6, IN_5, IN_4, IN_3, IN_2, IN_1, IN_0}), .en(LOAD), .Q(DEBUG), .clk(clock_1_out));  // open: clr
  DotMatrix #(.inputtype("row"), .matrixcols(12)) dotmatrix_1 ();  // open: row0, row1, row2, row3, row4, row5, row6
endmodule

module decoder (
  output _100_A,
  output _10_A,
  output _1_A,
  output _100_B,
  output _10_B,
  output _1_B,
  output _10_C,
  output _10_C_2,
  output _1_C,
  output _10_D,
  output _10_D_2,
  output _1_D,
  output _10_E,
  output _10_E_2,
  output _1_E,
  output _10_F,
  output _10_F_2,
  output _1_F,
  output _10_G,
  output _10_G_2,
  output _1_G,
  output _10_DOT,
  output _10_DOT_2,
  output _1_DOT
);
endmodule

module MAR (
  input  IN_0,
  input  IN_1,
  input  IN_2,
  input  IN_3,
  input  MI,
  input  CLK,
  output [3:0] DEBUG,
  output OUT_0,
  output OUT_1,
  output OUT_2,
  output OUT_3
);

  Register #(.width(4)) register_1 (.D({IN_3, IN_2, IN_1, IN_0}), .en(MI), .Q(DEBUG), .clk(CLK));  // open: clr

  assign OUT_0 = DEBUG[0];
  assign OUT_1 = DEBUG[1];
  assign OUT_2 = DEBUG[2];
  assign OUT_3 = DEBUG[3];
endmodule

module RAM (
  input  A_0,
  input  A_1,
  input  A_2,
  input  RO,
  input  A_3,
  input  RI,
  input  IN_0,
  input  IN_1,
  input  IN_2,
  input  IN_3,
  input  IN_4,
  input  IN_5,
  input  IN_6,
  input  IN_7,
  output OUT_0,
  output OUT_1,
  output OUT_2,
  output OUT_3,
  output OUT_4,
  output OUT_5,
  output [7:0] DEBUG,
  output OUT_6,
  output OUT_7
);

  wire clock_1_out;

  Clock clock_1 (.out(clock_1_out));
  RAM_part #(.addrWidth(4), .bus("separate")) ram_1 (
    .addr({A_3, A_2, A_1, A_0}), .din({IN_7, IN_6, IN_5, IN_4, IN_3, IN_2, IN_1, IN_0}), .data(DEBUG),
    .str(RI), .clk(clock_1_out));  // open: sel, ld, clr
  assign {OUT_7, OUT_6, OUT_5, OUT_4, OUT_3, OUT_2, OUT_1, OUT_0} = RO ? DEBUG : 8'bz;  // Controlled_Buffer controlled_buffer_1
endmodule

module IR (
  input  IN_0,
  input  IN_1,
  input  IN_2,
  input  IN_3,
  input  IN_4,
  input  IN_5,
  input  IN_6,
  input  II,
  input  CLK,
  input  IO,
  input  IN_7,
  output OUT_0,
  output [7:0] DEBUG,
  output OUT_1,
  output OUT_2,
  output OUT_3,
  output OUT_4,
  output OUT_5,
  output OUT_6,
  output OUT_7,
  output Q_0,
  output Q_1,
  output Q_2,
  output Q_3,
  output Q_4,
  output Q_5,
  output Q_6,
  output Q_7
);

  assign {OUT_7, OUT_6, OUT_5, OUT_4, OUT_3, OUT_2, OUT_1, OUT_0} = IO ? DEBUG : 8'bz;  // Controlled_Buffer controlled_buffer_1
  Register register_1 (
    .D({IN_7, IN_6, IN_5, IN_4, IN_3, IN_2, IN_1, IN_0}), .en(II), .Q(DEBUG), .clk(CLK));  // open: clr

  assign Q_0 = DEBUG[0];
  assign Q_1 = DEBUG[1];
  assign Q_2 = DEBUG[2];
  assign Q_3 = DEBUG[3];
  assign Q_4 = DEBUG[4];
  assign Q_5 = DEBUG[5];
  assign Q_6 = DEBUG[6];
  assign Q_7 = DEBUG[7];
endmodule

module CONTROL (
  input  IN_0,
  input  IN_1,
  input  IN_2,
  input  IN_3,
  input  IN_4,
  input  IN_5,
  input  IN_6,
  input  IN_7
);
endmodule
